# Fritzing sketch thermostat-recup (saved by Fritzing 0.9.2b)
breadboards: 1

parts:
  Composant2 = Arduino Nano (Rev3.0)
  Grove1 = Grove OLED 128x96
  R3 = Resistor [tolerance=±5% resistance=4.7k package=THT]
  S3 = Pushbutton [package="[THT]"]
  S4 = Momentary Switch [package=ksa_sealed_tac_switch]

nets:
  N1: Composant2.D2, S4.1
  N2: Composant2.D3, S3.Pin_1, S3.Pin_2
  N3: Composant2.D9, R3.Pin_0
  N4: Composant2.5V, R3.Pin_1
  3V3: Composant2.3V3, Grove1.VCC
  N5: Grove1.GND, S3.Pin_3, S3.Pin_4, S4.3

notes:
  sonde
  DS18B20
  s
  Relay
