# Fritzing sketch thermostatV2 (saved by Fritzing 0.9.2b)
breadboards: 1

parts:
  Composant2 = Arduino Nano (Rev3.0)
  Grove1 = Grove OLED 128x96
  R3 = Resistor [tolerance=±5% resistance=4.7k package=THT]
  S3 = Pushbutton [package="[THT]"]
  S4 = Momentary Switch [package=ksa_sealed_tac_switch]
  R4 = Resistor [tolerance=±5% resistance=2.2k package=THT]
  R5 = Resistor [tolerance=±5% resistance=220 package=THT]
  R6 = Resistor [tolerance=±5% resistance=220 package=THT]
  R7 = Resistor [tolerance=±5% resistance=220 package=THT]
  R8 = Resistor [tolerance=±5% resistance=220 package=THT]
  R9 = Resistor [tolerance=±5% resistance=220 package=THT]
  R10 = Resistor [tolerance=±5% resistance=220 package=THT]

nets:
  N1: Composant2.D2, S4.1
  N2: Composant2.D3, S3.Pin_1, S3.Pin_2
  N3: Composant2.D9, R3.Pin_0
  5V: Composant2.5V, Grove1.VCC, R3.Pin_1, R4.Pin_0
  N4: Composant2.A5, Grove1.SCL
  N5: Composant2.A4, Grove1.SDA
  N6: Composant2.A3, R4.Pin_1
  N7: Grove1.GND, S3.Pin_3, S3.Pin_4, S4.3, R5.Pin_1, R6.Pin_1, R7.Pin_1, R8.Pin_1, R9.Pin_1, R10.Pin_1

notes:
  sonde
  DS18B20
  NB: R4 = 2157Ω
  Relay
